# Fritzing sketch wiring (saved by Fritzing 0.9.9b)

parts:
  Part1 = Adafruit Feather ESP32-S2 [part_number="Adafruit #5000"]
  Part2 = Adafruit STEMMA Non-Latching Relay Breakout [part_number="Adafruit #4409"]
  U1 = TMP36 [package=to-92]
  C1 = Ceramic Capacitor [capacitance="100 nF" voltage=35V package="100 mil [THT, multilayer]"]

nets:
  N1: Part1.A5, U1.VOUT, C1.1
  GND: Part1.GND, Part2.GND, U1.GND, C1.0
  3.3V: Part1.3.3V, Part2.VIN, U1.VCC
  N2: Part1.D10, Part2.SIGNAL

notes:
  connect the relay to the R and W wires

custom parts:
  Adafruit Feather ESP32-S2: What's Feather-shaped and has an ESP32-S2 WiFi module? What has a STEMMA QT connector for I2C devices and a built in ambient sensor? What has your favorite Espressif WiFi microcontroller and lots of Flash and RAM memory for your next IoT project? What will make your next IoT project sensor project flyyyyy? That's right - it's the new Adafruit ESP32-S2 Feather and Adafruit ESP32-S2 Feather with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
  Adafruit STEMMA Non-Latching Relay Breakout: STEMMA plug-and-play parts make your next project soldering-free! This is the STEMMA Non-Latching Mini Relay. It gives you power to control, and control over power. Put simply, you can now turn on and off lamps, fans, solenoids, and other small appliances that run on up to 250VAC or DC power using any microcontroller or microcomputer, with ease. No worrying about flyback diodes, level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
